// Logisim project Offline1.circ as structural Verilog: 1 circuit, main circuit main
module main (
  input  S2,
  input  S1,
  input  S0,
  input  A0,
  input  B0,
  input  A1,
  input  B1,
  input  A2,
  input  B2,
  input  A3,
  input  B3,
  output F0,
  output F1,
  output F2,
  output F3,
  output C,
  output S,
  output Z,
  output V
);

  wire adder_1_cout, adder_2_cout, adder_3_cout, adder_4_cout, and_1_out, and_2_out, and_3_out, and_4_out,
       and_5_out, and_6_out, and_7_out, and_8_out, and_9_out, and_10_out, and_11_out, and_12_out, not_1_out,
       not_2_out, not_3_out, not_4_out, not_5_out, not_6_out, not_7_out, not_8_out, not_9_out, or_1_out,
       or_2_out, or_3_out, or_4_out, xor_1_out, xor_2_out, xor_3_out, xor_4_out, xor_5_out;

  not not_1 (not_1_out, S0);
  not not_2 (not_2_out, B0);
  not not_3 (not_3_out, S0);
  not not_4 (not_4_out, B1);
  not not_5 (not_5_out, S0);
  not not_6 (not_6_out, B2);
  not not_7 (not_7_out, S0);
  not not_8 (not_8_out, B3);
  xor xor_1 (xor_1_out, S1, B0);
  xor xor_2 (xor_2_out, S1, B1);
  xor xor_3 (xor_3_out, S1, B2);
  xor xor_4 (xor_4_out, S1, B3);
  and and_1 (and_1_out, S2, not_1_out);
  and and_2 (and_2_out, S0, xor_1_out);
  and and_3 (and_3_out, S1, not_2_out);
  and and_4 (and_4_out, adder_1_cout, not_3_out);
  and and_5 (and_5_out, S0, xor_2_out);
  and and_6 (and_6_out, S1, not_4_out);
  and and_7 (and_7_out, adder_2_cout, not_5_out);
  and and_8 (and_8_out, S0, xor_3_out);
  and and_9 (and_9_out, S1, not_6_out);
  and and_10 (and_10_out, adder_3_cout, not_7_out);
  and and_11 (and_11_out, S0, xor_4_out);
  and and_12 (and_12_out, S1, not_8_out);
  not not_9 (not_9_out, S0);
  or or_1 (or_1_out, and_2_out, A0);
  or or_2 (or_2_out, and_5_out, A1);
  or or_3 (or_3_out, and_8_out, A2);
  or or_4 (or_4_out, and_11_out, A3);
  Adder #(.width(1)) adder_1 (.a(or_1_out), .b(and_3_out), .out(F0), .cin(and_1_out), .cout(adder_1_cout));
  Adder #(.width(1)) adder_2 (.a(or_2_out), .b(and_6_out), .out(F1), .cin(and_4_out), .cout(adder_2_cout));
  Adder #(.width(1)) adder_3 (.a(or_3_out), .b(and_9_out), .out(F2), .cin(and_7_out), .cout(adder_3_cout));
  Adder #(.width(1)) adder_4 (.a(or_4_out), .b(and_12_out), .out(F3), .cin(and_10_out), .cout(adder_4_cout));
  and and_13 (C, adder_4_cout, not_9_out);
  nor nor_1 (Z, F3, F2, F1, F0);
  xor xor_5 (xor_5_out, and_10_out, adder_4_cout);
  and and_14 (V, xor_5_out, not_9_out);

  assign S = F3;
endmodule
