// Logisim project Offline 2.circ as structural Verilog: 7 circuits, main circuit main
module main (
  input  [15:0] in_1,
  input  in_2,
  input  [3:0] in_3,
  input  [15:0] in_4,
  output [12:0] out_5,
  output [3:0] out_6,
  output [15:0] out_7
);

  wire comparator_1_eq, comparator_2_eq, comparator_2_lt, nand_1_out, normalizer_1_out_2, normalizer_2_out_2,
       xor_1_out;
  wire [1:0] or_1_out;
  wire [3:0] adder_2_out, adder_3_out, multiplexer_2_out, multiplexer_3_out, negator_1_out_3,
       negator_2_out_3, normalizer_1_out_4, normalizer_2_out_4, subtractor_1_out, subtractor_2_out;
  wire [10:0] multiplexer_7_out;
  wire [11:0] shifter_1_out;
  wire [12:0] multiplexer_6_out, normalizer_2_out_3, rounder_1_out_3, selection_adder_1_out_3;
  wire [12:12] multiplexer_5_out;
  wire [15:0] and_1_out, bit_extender_1_out;
  wire [15:15] selection_adder_1_out_4;

  xor xor_1 (xor_1_out, in_1[15], in_4[15]);
  Multiplexer #(.select(2), .width(16), .enable("false")) multiplexer_1 (
    .in0({16{1'b0}}), .in1(in_4), .in2(in_1), .in3(and_1_out), .out(out_7), .sel(or_1_out));
  assign and_1_out = {selection_adder_1_out_4[15], adder_3_out, normalizer_2_out_3[10:0]} & bit_extender_1_out;  // AND_Gate and_1, 16 bits wide
  assign bit_extender_1_out = {{15{nand_1_out}}, nand_1_out};  // Bit_Extender bit_extender_1
  Comparator #(.width(11)) comparator_1 (.a(in_1[10:0]), .b(in_4[10:0]), .eq(comparator_1_eq));  // open: gt, lt
  Comparator #(.width(4), .mode("unsigned")) comparator_2 (
    .a(in_1[14:11]), .b(in_4[14:11]), .eq(comparator_2_eq), .lt(comparator_2_lt));  // open: gt
  nand nand_1 (nand_1_out, comparator_1_eq, xor_1_out, comparator_2_eq);
  or or_1 (or_1_out[0], in_4[15], in_4[14], in_4[13], in_4[12], in_4[11], in_4[10], in_4[9], in_4[8], in_4[7], in_4[6], in_4[5], in_4[4], in_4[3], in_4[2], in_4[1], in_4[0]);
  Multiplexer #(.width(4), .enable("false")) multiplexer_2 (
    .in0(in_1[14:11]), .in1(in_4[14:11]), .out(multiplexer_2_out), .sel(comparator_2_lt));
  Multiplexer #(.width(4), .enable("false")) multiplexer_3 (
    .in0(in_4[14:11]), .in1(in_1[14:11]), .out(multiplexer_3_out), .sel(comparator_2_lt));
  Subtractor #(.width(4)) subtractor_1 (
    .a(multiplexer_2_out), .b(multiplexer_3_out), .out(subtractor_1_out), .bin(in_2));  // open: bout
  or or_2 (or_1_out[1], in_1[15], in_1[14], in_1[13], in_1[12], in_1[11], in_1[10], in_1[9], in_1[8], in_1[7], in_1[6], in_1[5], in_1[4], in_1[3], in_1[2], in_1[1], in_1[0]);
  Multiplexer #(.enable("false")) multiplexer_4 (
    .in0(in_1[15]), .in1(in_4[15]), .out(multiplexer_6_out[12]), .sel(comparator_2_lt));
  Multiplexer #(.enable("false")) multiplexer_5 (
    .in0(in_4[15]), .in1(in_1[15]), .out(multiplexer_5_out[12]), .sel(comparator_2_lt));
  Multiplexer #(.width(11), .enable("false")) multiplexer_6 (
    .in0(in_1[10:0]), .in1(in_4[10:0]), .out(multiplexer_6_out[10:0]), .sel(comparator_2_lt));
  Multiplexer #(.width(11), .enable("false")) multiplexer_7 (
    .in0(in_4[10:0]), .in1(in_1[10:0]), .out(multiplexer_7_out), .sel(comparator_2_lt));
  Shifter #(.width(12), .shift("lr")) shifter_1 (
    .in({1'b1, multiplexer_7_out}), .\dist (subtractor_1_out), .out(shifter_1_out));
  Selection_adder selection_adder_1 (
    .in_1({multiplexer_6_out[12], 1'b1, multiplexer_6_out[10:0]}),
    .in_2({multiplexer_5_out[12], shifter_1_out}), .out_3(selection_adder_1_out_3),
    .out_4(selection_adder_1_out_4[15]));
  Normalizer normalizer_1 (
    .out_2(normalizer_1_out_2), .in_1(selection_adder_1_out_3), .out_4(normalizer_1_out_4), .out_3(out_5));
  negator negator_1 (.in_1(normalizer_1_out_4), .in_2(normalizer_1_out_2), .out_3(negator_1_out_3));
  Subtractor #(.width(4)) subtractor_2 (.a(multiplexer_2_out), .b(4'b0111), .out(subtractor_2_out));  // open: bin, bout
  Adder #(.width(4)) adder_1 (.a(subtractor_2_out), .b(negator_1_out_3), .out(out_6));  // open: cin, cout
  Rounder rounder_1 (.in_1(out_5), .in_2(in_3), .out_3(rounder_1_out_3));
  Normalizer normalizer_2 (
    .out_2(normalizer_2_out_2), .in_1(rounder_1_out_3), .out_4(normalizer_2_out_4), .out_3(normalizer_2_out_3));
  Adder #(.width(4)) adder_2 (.a(out_6), .b(negator_2_out_3), .out(adder_2_out));  // open: cin, cout
  Adder #(.width(4)) adder_3 (.a(adder_2_out), .b(4'b0111), .out(adder_3_out));  // open: cin, cout
  negator negator_2 (.in_1(normalizer_2_out_4), .in_2(normalizer_2_out_2), .out_3(negator_2_out_3));
endmodule

module Normalizer (
  input  [12:0] in_1,
  output out_2,
  output [12:0] out_3,
  output [3:0] out_4
);

  wire comparator_3_eq;
  wire [0:0] comparator_1_eq, comparator_2_eq;
  wire [1:1] comparator_4_eq, comparator_5_eq;
  wire [2:2] comparator_6_eq, comparator_7_eq, comparator_8_eq;
  wire [3:0] and_1_out, and_4_out, and_5_out, and_6_out, and_10_out, and_12_out, and_13_out, and_15_out,
       and_16_out, and_17_out, and_18_out, and_20_out, and_21_out, and_23_out, and_24_out, and_26_out,
       and_27_out, and_28_out, and_29_out, and_31_out, and_32_out, and_34_out, and_35_out, and_36_out,
       and_37_out, bit_extender_1_out, bit_extender_2_out, bit_extender_3_out, bit_extender_4_out,
       bit_extender_5_out, bit_extender_6_out, bit_extender_7_out, bit_extender_8_out, bit_extender_9_out,
       bit_extender_10_out, bit_extender_11_out, bit_extender_12_out, bit_extender_13_out, not_1_out,
       not_2_out, not_4_out, not_5_out, not_6_out, not_7_out, not_8_out, not_9_out, not_10_out, not_11_out,
       not_12_out, not_13_out, or_2_out, or_3_out, or_4_out, or_5_out, or_6_out, or_7_out, or_8_out,
       or_9_out, or_10_out, or_11_out, or_12_out;
  wire [3:3] comparator_9_eq, comparator_10_eq, comparator_11_eq, comparator_12_eq, comparator_13_eq;
  wire [12:0] and_2_out, and_3_out, and_7_out, and_8_out, and_9_out, and_11_out, and_14_out, and_19_out,
       and_22_out, and_25_out, and_30_out, and_33_out, and_38_out, and_39_out, and_40_out, and_41_out,
       and_42_out, and_43_out, and_44_out, and_45_out, and_46_out, and_47_out, and_48_out, and_49_out,
       and_50_out, n1_to_13_bit_1_out_2, n1_to_13_bit_2_out_2, n1_to_13_bit_3_out_2, n1_to_13_bit_4_out_2,
       n1_to_13_bit_5_out_2, n1_to_13_bit_6_out_2, n1_to_13_bit_7_out_2, n1_to_13_bit_8_out_2,
       n1_to_13_bit_9_out_2, n1_to_13_bit_10_out_2, n1_to_13_bit_11_out_2, n1_to_13_bit_12_out_2,
       n1_to_13_bit_13_out_2, not_3_out, not_14_out, not_15_out, not_16_out, not_17_out, not_18_out,
       not_19_out, not_20_out, not_21_out, not_22_out, not_23_out, not_24_out, or_13_out, or_14_out,
       or_15_out, or_16_out, or_17_out, or_18_out, or_19_out, or_20_out, or_21_out, or_22_out, or_23_out,
       shifter_1_out, shifter_2_out, shifter_3_out, shifter_4_out, shifter_5_out, shifter_6_out,
       shifter_7_out, shifter_8_out, shifter_9_out, shifter_10_out, shifter_11_out, shifter_12_out;

  nor nor_1 (out_2, in_1[12], in_1[11]);
  Comparator #(.width(1)) comparator_1 (.a(in_1[12]), .b(1'b1), .eq(comparator_1_eq[0]));  // open: gt, lt
  Comparator #(.width(1)) comparator_2 (.a(in_1[10]), .b(1'b1), .eq(comparator_2_eq[0]));  // open: gt, lt
  Comparator #(.width(1)) comparator_3 (.a(in_1[11]), .b(1'b1), .eq(comparator_3_eq));  // open: gt, lt
  Shifter #(.width(13), .shift("lr")) shifter_1 (.in(in_1), .\dist ({3'b000, comparator_1_eq[0]}), .out(shifter_1_out));
  assign and_1_out = {3'b000, comparator_1_eq[0]} & bit_extender_2_out;  // AND_Gate and_1, 4 bits wide
  Comparator #(.width(1)) comparator_4 (.a(in_1[9]), .b(1'b1), .eq(comparator_4_eq[1]));  // open: gt, lt
  _1_to_13_bit u_1_to_13_bit_1 (.in_1(comparator_3_eq), .out_2(n1_to_13_bit_1_out_2));
  assign bit_extender_1_out = {{3{comparator_3_eq}}, comparator_3_eq};  // Bit_Extender bit_extender_1
  _1_to_13_bit u_1_to_13_bit_2 (.in_1(in_1[12]), .out_2(n1_to_13_bit_2_out_2));
  assign bit_extender_2_out = {{3{in_1[12]}}, in_1[12]};  // Bit_Extender bit_extender_2
  assign out_4 = and_1_out | and_5_out;  // OR_Gate or_1, 4 bits wide
  Shifter #(.width(13)) shifter_2 (.in(in_1), .\dist ({3'b000, comparator_2_eq[0]}), .out(shifter_2_out));
  assign and_2_out = in_1 & n1_to_13_bit_1_out_2;  // AND_Gate and_2, 13 bits wide
  assign and_3_out = shifter_1_out & n1_to_13_bit_2_out_2;  // AND_Gate and_3, 13 bits wide
  _1_to_13_bit u_1_to_13_bit_3 (.in_1(in_1[10]), .out_2(n1_to_13_bit_3_out_2));
  assign and_4_out = 4'b0000 & bit_extender_1_out;  // AND_Gate and_4, 4 bits wide
  assign not_1_out = ~bit_extender_2_out;  // NOT_Gate not_1, 4 bits wide
  assign and_5_out = not_1_out & or_2_out;  // AND_Gate and_5, 4 bits wide
  Comparator #(.width(1)) comparator_5 (.a(in_1[8]), .b(1'b1), .eq(comparator_5_eq[1]));  // open: gt, lt
  Shifter #(.width(13)) shifter_3 (.in(in_1), .\dist ({2'b00, comparator_4_eq[1], 1'b0}), .out(shifter_3_out));
  assign not_2_out = ~bit_extender_1_out;  // NOT_Gate not_2, 4 bits wide
  assign and_6_out = not_2_out & or_3_out;  // AND_Gate and_6, 4 bits wide
  assign or_2_out = and_4_out | and_6_out;  // OR_Gate or_2, 4 bits wide
  assign and_7_out = shifter_2_out & n1_to_13_bit_3_out_2;  // AND_Gate and_7, 13 bits wide
  Comparator #(.width(1)) comparator_6 (.a(in_1[7]), .b(1'b1), .eq(comparator_6_eq[2]));  // open: gt, lt
  Shifter #(.width(13)) shifter_4 (.in(in_1), .\dist ({2'b00, {2{comparator_5_eq[1]}}}), .out(shifter_4_out));
  _1_to_13_bit u_1_to_13_bit_4 (.in_1(in_1[9]), .out_2(n1_to_13_bit_4_out_2));
  Comparator #(.width(1)) comparator_7 (.a(in_1[6]), .b(1'b1), .eq(comparator_7_eq[2]));  // open: gt, lt
  assign and_8_out = shifter_3_out & n1_to_13_bit_4_out_2;  // AND_Gate and_8, 13 bits wide
  Shifter #(.width(13)) shifter_5 (.in(in_1), .\dist ({1'b0, comparator_6_eq[2], 2'b00}), .out(shifter_5_out));
  _1_to_13_bit u_1_to_13_bit_5 (.in_1(in_1[8]), .out_2(n1_to_13_bit_5_out_2));
  Comparator #(.width(1)) comparator_8 (.a(in_1[5]), .b(1'b1), .eq(comparator_8_eq[2]));  // open: gt, lt
  assign bit_extender_3_out = {{3{in_1[10]}}, in_1[10]};  // Bit_Extender bit_extender_3
  Comparator #(.width(1)) comparator_9 (.a(in_1[4]), .b(1'b1), .eq(comparator_9_eq[3]));  // open: gt, lt
  Shifter #(.width(13)) shifter_6 (
    .in(in_1), .\dist ({1'b0, comparator_7_eq[2], 1'b0, comparator_7_eq[2]}), .out(shifter_6_out));
  assign and_9_out = shifter_4_out & n1_to_13_bit_5_out_2;  // AND_Gate and_9, 13 bits wide
  assign and_10_out = {3'b000, comparator_2_eq[0]} & bit_extender_3_out;  // AND_Gate and_10, 4 bits wide
  Shifter #(.width(13)) shifter_7 (.in(in_1), .\dist ({1'b0, {3{comparator_8_eq[2]}}}), .out(shifter_7_out));
  _1_to_13_bit u_1_to_13_bit_6 (.in_1(in_1[6]), .out_2(n1_to_13_bit_6_out_2));
  _1_to_13_bit u_1_to_13_bit_7 (.in_1(in_1[7]), .out_2(n1_to_13_bit_7_out_2));
  assign bit_extender_4_out = {{3{in_1[9]}}, in_1[9]};  // Bit_Extender bit_extender_4
  assign not_3_out = ~n1_to_13_bit_2_out_2;  // NOT_Gate not_3, 13 bits wide
  assign not_4_out = ~bit_extender_3_out;  // NOT_Gate not_4, 4 bits wide
  assign or_3_out = and_10_out | and_13_out;  // OR_Gate or_3, 4 bits wide
  Comparator #(.width(1)) comparator_10 (.a(in_1[3]), .b(1'b1), .eq(comparator_10_eq[3]));  // open: gt, lt
  assign and_11_out = shifter_5_out & n1_to_13_bit_7_out_2;  // AND_Gate and_11, 13 bits wide
  assign bit_extender_5_out = {{3{in_1[7]}}, in_1[7]};  // Bit_Extender bit_extender_5
  assign and_12_out = {2'b00, comparator_4_eq[1], 1'b0} & bit_extender_4_out;  // AND_Gate and_12, 4 bits wide
  assign or_4_out = and_12_out | and_16_out;  // OR_Gate or_4, 4 bits wide
  assign and_13_out = not_4_out & or_4_out;  // AND_Gate and_13, 4 bits wide
  Shifter #(.width(13)) shifter_8 (.in(in_1), .\dist ({comparator_9_eq[3], 3'b000}), .out(shifter_8_out));
  _1_to_13_bit u_1_to_13_bit_8 (.in_1(in_1[5]), .out_2(n1_to_13_bit_8_out_2));
  assign and_14_out = shifter_6_out & n1_to_13_bit_6_out_2;  // AND_Gate and_14, 13 bits wide
  assign bit_extender_6_out = {{3{in_1[8]}}, in_1[8]};  // Bit_Extender bit_extender_6
  assign and_15_out = {2'b00, {2{comparator_5_eq[1]}}} & bit_extender_6_out;  // AND_Gate and_15, 4 bits wide
  assign or_5_out = and_15_out | and_18_out;  // OR_Gate or_5, 4 bits wide
  assign not_5_out = ~bit_extender_4_out;  // NOT_Gate not_5, 4 bits wide
  assign and_16_out = not_5_out & or_5_out;  // AND_Gate and_16, 4 bits wide
  Comparator #(.width(1)) comparator_11 (.a(in_1[2]), .b(1'b1), .eq(comparator_11_eq[3]));  // open: gt, lt
  Shifter #(.width(13)) shifter_9 (
    .in(in_1), .\dist ({comparator_10_eq[3], 2'b00, comparator_10_eq[3]}), .out(shifter_9_out));
  _1_to_13_bit u_1_to_13_bit_9 (.in_1(in_1[4]), .out_2(n1_to_13_bit_9_out_2));
  assign bit_extender_7_out = {{3{in_1[6]}}, in_1[6]};  // Bit_Extender bit_extender_7
  assign not_6_out = ~bit_extender_5_out;  // NOT_Gate not_6, 4 bits wide
  assign and_17_out = {1'b0, comparator_6_eq[2], 2'b00} & bit_extender_5_out;  // AND_Gate and_17, 4 bits wide
  assign or_6_out = and_17_out | and_21_out;  // OR_Gate or_6, 4 bits wide
  assign not_7_out = ~bit_extender_6_out;  // NOT_Gate not_7, 4 bits wide
  assign and_18_out = not_7_out & or_6_out;  // AND_Gate and_18, 4 bits wide
  assign bit_extender_8_out = {{3{in_1[4]}}, in_1[4]};  // Bit_Extender bit_extender_8
  assign and_19_out = shifter_7_out & n1_to_13_bit_8_out_2;  // AND_Gate and_19, 13 bits wide
  assign bit_extender_9_out = {{3{in_1[5]}}, in_1[5]};  // Bit_Extender bit_extender_9
  assign and_20_out = {1'b0, comparator_7_eq[2], 1'b0, comparator_7_eq[2]} & bit_extender_7_out;  // AND_Gate and_20, 4 bits wide
  assign or_7_out = and_20_out | and_24_out;  // OR_Gate or_7, 4 bits wide
  assign and_21_out = not_6_out & or_7_out;  // AND_Gate and_21, 4 bits wide
  Comparator #(.width(1)) comparator_12 (.a(in_1[1]), .b(1'b1), .eq(comparator_12_eq[3]));  // open: gt, lt
  Shifter #(.width(13)) shifter_10 (
    .in(in_1), .\dist ({comparator_11_eq[3], 1'b0, comparator_11_eq[3], 1'b0}), .out(shifter_10_out));
  _1_to_13_bit u_1_to_13_bit_10 (.in_1(in_1[3]), .out_2(n1_to_13_bit_10_out_2));
  assign and_22_out = shifter_8_out & n1_to_13_bit_9_out_2;  // AND_Gate and_22, 13 bits wide
  assign and_23_out = {1'b0, {3{comparator_8_eq[2]}}} & bit_extender_9_out;  // AND_Gate and_23, 4 bits wide
  assign or_8_out = and_23_out | and_27_out;  // OR_Gate or_8, 4 bits wide
  assign not_8_out = ~bit_extender_7_out;  // NOT_Gate not_8, 4 bits wide
  assign and_24_out = not_8_out & or_8_out;  // AND_Gate and_24, 4 bits wide
  Comparator #(.width(1)) comparator_13 (.a(in_1[0]), .b(1'b1), .eq(comparator_13_eq[3]));  // open: gt, lt
  Shifter #(.width(13)) shifter_11 (
    .in(in_1), .\dist ({comparator_12_eq[3], 1'b0, {2{comparator_12_eq[3]}}}), .out(shifter_11_out));
  _1_to_13_bit u_1_to_13_bit_11 (.in_1(in_1[2]), .out_2(n1_to_13_bit_11_out_2));
  assign and_25_out = shifter_9_out & n1_to_13_bit_10_out_2;  // AND_Gate and_25, 13 bits wide
  assign bit_extender_10_out = {{3{in_1[3]}}, in_1[3]};  // Bit_Extender bit_extender_10
  assign not_9_out = ~bit_extender_8_out;  // NOT_Gate not_9, 4 bits wide
  assign and_26_out = {comparator_9_eq[3], 3'b000} & bit_extender_8_out;  // AND_Gate and_26, 4 bits wide
  assign or_9_out = and_26_out | and_29_out;  // OR_Gate or_9, 4 bits wide
  assign not_10_out = ~bit_extender_9_out;  // NOT_Gate not_10, 4 bits wide
  assign and_27_out = not_10_out & or_9_out;  // AND_Gate and_27, 4 bits wide
  assign bit_extender_11_out = {{3{in_1[2]}}, in_1[2]};  // Bit_Extender bit_extender_11
  assign and_28_out = {comparator_10_eq[3], 2'b00, comparator_10_eq[3]} & bit_extender_10_out;  // AND_Gate and_28, 4 bits wide
  assign or_10_out = and_28_out | and_32_out;  // OR_Gate or_10, 4 bits wide
  assign and_29_out = not_9_out & or_10_out;  // AND_Gate and_29, 4 bits wide
  Shifter #(.width(13)) shifter_12 (.in(in_1), .\dist ({{2{comparator_13_eq[3]}}, 2'b00}), .out(shifter_12_out));
  _1_to_13_bit u_1_to_13_bit_12 (.in_1(in_1[1]), .out_2(n1_to_13_bit_12_out_2));
  assign and_30_out = shifter_10_out & n1_to_13_bit_11_out_2;  // AND_Gate and_30, 13 bits wide
  assign and_31_out = {comparator_11_eq[3], 1'b0, comparator_11_eq[3], 1'b0} & bit_extender_11_out;  // AND_Gate and_31, 4 bits wide
  assign not_11_out = ~bit_extender_10_out;  // NOT_Gate not_11, 4 bits wide
  assign and_32_out = not_11_out & or_12_out;  // AND_Gate and_32, 4 bits wide
  assign and_33_out = shifter_11_out & n1_to_13_bit_12_out_2;  // AND_Gate and_33, 13 bits wide
  assign bit_extender_12_out = {{3{in_1[1]}}, in_1[1]};  // Bit_Extender bit_extender_12
  assign and_34_out = {comparator_12_eq[3], 1'b0, {2{comparator_12_eq[3]}}} & bit_extender_12_out;  // AND_Gate and_34, 4 bits wide
  assign or_11_out = and_34_out | and_37_out;  // OR_Gate or_11, 4 bits wide
  assign not_12_out = ~bit_extender_11_out;  // NOT_Gate not_12, 4 bits wide
  assign and_35_out = not_12_out & or_11_out;  // AND_Gate and_35, 4 bits wide
  assign or_12_out = and_31_out | and_35_out;  // OR_Gate or_12, 4 bits wide
  _1_to_13_bit u_1_to_13_bit_13 (.in_1(in_1[0]), .out_2(n1_to_13_bit_13_out_2));
  assign bit_extender_13_out = {{3{in_1[0]}}, in_1[0]};  // Bit_Extender bit_extender_13
  assign and_36_out = {{2{comparator_13_eq[3]}}, 2'b00} & bit_extender_13_out;  // AND_Gate and_36, 4 bits wide
  assign not_13_out = ~bit_extender_12_out;  // NOT_Gate not_13, 4 bits wide
  assign and_37_out = not_13_out & and_36_out;  // AND_Gate and_37, 4 bits wide
  assign and_38_out = shifter_12_out & n1_to_13_bit_13_out_2;  // AND_Gate and_38, 13 bits wide
  assign not_14_out = ~n1_to_13_bit_5_out_2;  // NOT_Gate not_14, 13 bits wide
  assign not_15_out = ~n1_to_13_bit_4_out_2;  // NOT_Gate not_15, 13 bits wide
  assign not_16_out = ~n1_to_13_bit_3_out_2;  // NOT_Gate not_16, 13 bits wide
  assign not_17_out = ~n1_to_13_bit_12_out_2;  // NOT_Gate not_17, 13 bits wide
  assign not_18_out = ~n1_to_13_bit_7_out_2;  // NOT_Gate not_18, 13 bits wide
  assign not_19_out = ~n1_to_13_bit_1_out_2;  // NOT_Gate not_19, 13 bits wide
  assign and_39_out = and_38_out & not_17_out;  // AND_Gate and_39, 13 bits wide
  assign not_20_out = ~n1_to_13_bit_11_out_2;  // NOT_Gate not_20, 13 bits wide
  assign or_13_out = and_39_out | and_33_out;  // OR_Gate or_13, 13 bits wide
  assign and_40_out = or_13_out & not_20_out;  // AND_Gate and_40, 13 bits wide
  assign not_21_out = ~n1_to_13_bit_6_out_2;  // NOT_Gate not_21, 13 bits wide
  assign not_22_out = ~n1_to_13_bit_10_out_2;  // NOT_Gate not_22, 13 bits wide
  assign or_14_out = and_40_out | and_30_out;  // OR_Gate or_14, 13 bits wide
  assign and_41_out = or_14_out & not_22_out;  // AND_Gate and_41, 13 bits wide
  assign not_23_out = ~n1_to_13_bit_9_out_2;  // NOT_Gate not_23, 13 bits wide
  assign not_24_out = ~n1_to_13_bit_8_out_2;  // NOT_Gate not_24, 13 bits wide
  assign or_15_out = and_41_out | and_25_out;  // OR_Gate or_15, 13 bits wide
  assign and_42_out = or_15_out & not_23_out;  // AND_Gate and_42, 13 bits wide
  assign or_16_out = and_42_out | and_22_out;  // OR_Gate or_16, 13 bits wide
  assign and_43_out = or_16_out & not_24_out;  // AND_Gate and_43, 13 bits wide
  assign or_17_out = and_43_out | and_19_out;  // OR_Gate or_17, 13 bits wide
  assign and_44_out = or_17_out & not_21_out;  // AND_Gate and_44, 13 bits wide
  assign or_18_out = and_44_out | and_14_out;  // OR_Gate or_18, 13 bits wide
  assign and_45_out = or_18_out & not_18_out;  // AND_Gate and_45, 13 bits wide
  assign or_19_out = and_45_out | and_11_out;  // OR_Gate or_19, 13 bits wide
  assign and_46_out = or_19_out & not_14_out;  // AND_Gate and_46, 13 bits wide
  assign or_20_out = and_46_out | and_9_out;  // OR_Gate or_20, 13 bits wide
  assign and_47_out = or_20_out & not_15_out;  // AND_Gate and_47, 13 bits wide
  assign or_21_out = and_47_out | and_8_out;  // OR_Gate or_21, 13 bits wide
  assign and_48_out = or_21_out & not_16_out;  // AND_Gate and_48, 13 bits wide
  assign or_22_out = and_48_out | and_7_out;  // OR_Gate or_22, 13 bits wide
  assign and_49_out = or_22_out & not_19_out;  // AND_Gate and_49, 13 bits wide
  assign or_23_out = and_49_out | and_2_out;  // OR_Gate or_23, 13 bits wide
  assign and_50_out = or_23_out & not_3_out;  // AND_Gate and_50, 13 bits wide
  assign out_3 = and_50_out | and_3_out;  // OR_Gate or_24, 13 bits wide
endmodule

module _1_to_13_bit (
  input  in_1,
  output [12:0] out_2
);


  assign out_2 = {13{in_1}};
endmodule

module negator (
  input  [3:0] in_1,
  input  in_2,
  output [3:0] out_3
);

  wire [3:0] adder_1_out, bit_extender_1_out, not_1_out;

  assign not_1_out = ~in_1;  // NOT_Gate not_1, 4 bits wide
  assign bit_extender_1_out = {{3{1'b0}}, 1'b1};  // Bit_Extender bit_extender_1
  Adder #(.width(4)) adder_1 (.a(not_1_out), .b(bit_extender_1_out), .out(adder_1_out), .cin(1'b0));  // open: cout
  Multiplexer #(.width(4), .enable("false")) multiplexer_1 (.in0(in_1), .in1(adder_1_out), .out(out_3), .sel(in_2));
endmodule

module neg (
  input  [3:0] in_1,
  output [3:0] out_2
);

  wire [3:0] bit_extender_1_out, not_1_out;

  assign not_1_out = ~in_1;  // NOT_Gate not_1, 4 bits wide
  assign bit_extender_1_out = {{3{1'b0}}, 1'b1};  // Bit_Extender bit_extender_1
  Adder #(.width(4)) adder_1 (.a(not_1_out), .b(bit_extender_1_out), .out(out_2), .cin(1'b0));  // open: cout
endmodule

module Rounder (
  input  [12:0] in_1,
  input  [3:0] in_2,
  output [12:0] out_3
);

  wire nor_1_out;
  wire [3:0] adder_1_out, multiplexer_2_out, subtractor_1_out;
  wire [12:0] adder_2_out, multiplexer_1_out, shifter_1_out, shifter_2_out;

  Multiplexer #(.width(13), .enable("false")) multiplexer_1 (
    .in0(13'h800), .in1({13{1'b0}}), .out(multiplexer_1_out), .sel(nor_1_out));
  nor nor_1 (nor_1_out, in_2[0], in_2[1], in_2[2], in_2[3]);
  Shifter #(.width(13), .shift("lr")) shifter_1 (.in(multiplexer_1_out), .\dist (in_2), .out(shifter_1_out));
  Adder #(.width(4)) adder_1 (.a(4'b0010), .b(in_2), .out(adder_1_out));  // open: cin, cout
  Adder #(.width(13)) adder_2 (.a(in_1), .b(shifter_1_out), .out(adder_2_out));  // open: cin, cout
  Subtractor #(.width(4)) subtractor_1 (.a(4'b1101), .b(adder_1_out), .out(subtractor_1_out));  // open: bin, bout
  Multiplexer #(.width(4), .enable("false")) multiplexer_2 (
    .in0(subtractor_1_out), .in1(in_2), .out(multiplexer_2_out), .sel(nor_1_out));
  assign out_3 = adder_2_out & shifter_2_out;  // AND_Gate and_1, 13 bits wide
  Shifter #(.width(13)) shifter_2 (.in({13{1'b1}}), .\dist (multiplexer_2_out), .out(shifter_2_out));
endmodule

module Selection_adder (
  input  [12:0] in_1,
  input  [12:0] in_2,
  output [12:0] out_3,
  output out_4
);

  wire not_1_out, xor_1_out;
  wire [11:0] adder_2_out, bit_extender_1_out, bit_extender_2_out, subtractor_1_out_2, xor_2_out;
  wire [12:0] adder_1_out, bit_extender_3_out, multiplexer_1_out, multiplexer_2_out;
  wire [12:12] subtractor_1_out;

  Multiplexer #(.width(13), .enable("false")) multiplexer_1 (
    .in0({1'b0, in_1[11:0]}), .in1({1'b0, in_2[11:0]}), .out(multiplexer_1_out), .sel(in_1[12]));
  Multiplexer #(.width(13), .enable("false")) multiplexer_2 (
    .in0({1'b0, in_1[11:0]}), .in1({1'b0, in_2[11:0]}), .out(multiplexer_2_out), .sel(not_1_out));
  not not_1 (not_1_out, in_1[12]);
  xor xor_1 (xor_1_out, in_2[12], in_1[12]);
  Adder #(.width(13)) adder_1 (
    .a(multiplexer_1_out), .b(multiplexer_2_out), .out(adder_1_out), .cin(1'b0));  // open: cout
  Subtractor #(.width(13)) subtractor_1 (
    .a(multiplexer_1_out), .b(multiplexer_2_out), .out({subtractor_1_out[12], subtractor_1_out_2}), .bin(1'b0));  // open: bout
  assign bit_extender_1_out = {{11{subtractor_1_out_2[11]}}, subtractor_1_out_2[11]};  // Bit_Extender bit_extender_1
  assign xor_2_out = subtractor_1_out_2 ^ bit_extender_1_out;  // XOR_Gate xor_2, 12 bits wide
  assign bit_extender_2_out = {{11{1'b0}}, subtractor_1_out_2[11]};  // Bit_Extender bit_extender_2
  Adder #(.width(12)) adder_2 (.a(xor_2_out), .b(bit_extender_2_out), .out(adder_2_out));  // open: cin, cout
  assign bit_extender_3_out = {{1{1'b0}}, adder_2_out};  // Bit_Extender bit_extender_3
  Multiplexer #(.width(13), .enable("false")) multiplexer_3 (
    .in0(adder_1_out), .in1(bit_extender_3_out), .out(out_3), .sel(xor_1_out));
  Multiplexer #(.enable("false")) multiplexer_4 (.in0(in_2[12]), .in1(in_1[12]), .out(out_4), .sel(xor_1_out));
endmodule
