// Logisim project Offline3.circ as structural Verilog: 7 circuits, main circuit main
module Register_File (
  input  [3:0] Rs,
  input  [3:0] Rt,
  input  [3:0] Rd,
  input  [7:0] WriteData,
  input  RegWrite,
  output [7:0] Read_Data_1,
  output [7:0] Read_Data_2
);

  wire clock_1_out;
  wire [5:0] and_1_out, bit_extender_1_out, decoder_1_out1;
  wire [7:0] multiplexer_1_out, multiplexer_2_out, multiplexer_3_out, multiplexer_4_out, multiplexer_5_out,
       multiplexer_6_out, sp_q, t0_q, t1_q, t2_q, t3_q, t4_q, zero_q;

  Decoder #(.select(4), .enable("false")) decoder_1 (
    .out1(decoder_1_out1[0]), .out2(decoder_1_out1[1]), .out3(decoder_1_out1[2]), .out4(decoder_1_out1[3]),
    .out5(decoder_1_out1[4]), .out6(decoder_1_out1[5]), .sel(Rd));  // open: out0, out7, out8, out9, out10, out11, out12, out13, out14, out15
  assign bit_extender_1_out = {{5{RegWrite}}, RegWrite};  // Bit_Extender bit_extender_1
  assign and_1_out = decoder_1_out1 & bit_extender_1_out;  // AND_Gate and_1, 6 bits wide
  Multiplexer #(.width(8), .enable("false")) multiplexer_1 (
    .in0(t0_q), .in1(WriteData), .out(multiplexer_1_out), .sel(and_1_out[0]));
  Multiplexer #(.width(8), .enable("false")) multiplexer_2 (
    .in0(t1_q), .in1(WriteData), .out(multiplexer_2_out), .sel(and_1_out[1]));
  Multiplexer #(.width(8), .enable("false")) multiplexer_3 (
    .in0(t2_q), .in1(WriteData), .out(multiplexer_3_out), .sel(and_1_out[2]));
  Clock clock_1 (.out(clock_1_out));
  Register zero (.D({8{1'b0}}), .Q(zero_q), .clk(clock_1_out));  // open: en, clr
  Register t0 (.D(multiplexer_1_out), .Q(t0_q), .clk(clock_1_out));  // open: en, clr
  Register t1 (.D(multiplexer_2_out), .Q(t1_q), .clk(clock_1_out));  // open: en, clr
  Register t2 (.D(multiplexer_3_out), .Q(t2_q), .clk(clock_1_out));  // open: en, clr
  Multiplexer #(.width(8), .enable("false")) multiplexer_4 (
    .in0(t3_q), .in1(WriteData), .out(multiplexer_4_out), .sel(and_1_out[3]));
  Multiplexer #(.width(8), .enable("false")) multiplexer_5 (
    .in0(t4_q), .in1(WriteData), .out(multiplexer_5_out), .sel(and_1_out[4]));
  Multiplexer #(.width(8), .enable("false")) multiplexer_6 (
    .in0(sp_q), .in1(WriteData), .out(multiplexer_6_out), .sel(and_1_out[5]));
  Register t3 (.D(multiplexer_4_out), .Q(t3_q), .clk(clock_1_out));  // open: en, clr
  Register t4 (.D(multiplexer_5_out), .Q(t4_q), .clk(clock_1_out));  // open: en, clr
  Register sp (.D(multiplexer_6_out), .Q(sp_q), .clk(clock_1_out));  // open: en, clr
  Multiplexer #(.select(4), .width(8), .enable("false")) multiplexer_7 (
    .in0(zero_q), .in1(t0_q), .in2(t1_q), .in3(t2_q), .in4(t3_q), .in5(t4_q), .in6(sp_q), .out(Read_Data_1),
    .sel(Rs));  // open: in7, in8, in9, in10, in11, in12, in13, in14, in15
  Multiplexer #(.select(4), .width(8), .enable("false")) multiplexer_8 (
    .in0(zero_q), .in1(t0_q), .in2(t1_q), .in3(t2_q), .in4(t3_q), .in5(t4_q), .in6(sp_q), .out(Read_Data_2),
    .sel(Rt));  // open: in7, in8, in9, in10, in11, in12, in13, in14, in15
endmodule

module main (
  output [7:0] out_1,
  output [7:0] out_2,
  output [7:0] out_3,
  output [7:0] Rs,
  output [7:0] out_5,
  output [19:0] out_6,
  output [7:0] out_7
);

  wire alu_1_zero, and_1_out, and_2_out, clock_1_out, cu_1_alusrc, cu_1_branch, cu_1_branchneq, cu_1_jump,
       cu_1_memread, cu_1_memtoreg, cu_1_memwrite, cu_1_regdst, cu_1_regwrite, isshift_1_out_2, not_1_out;
  wire [2:0] alu_1_out_6, cu_1_aluop;
  wire [3:0] multiplexer_2_out;
  wire [7:0] adder_1_out, alu_1_alu_result, bit_extender_1_out, data_memory_unit_1_read_data,
       multiplexer_1_out, multiplexer_3_out, multiplexer_5_out, multiplexer_6_out, multiplexer_7_out;

  Clock clock_1 (.out(clock_1_out));
  Register register_1 (.D(out_1), .Q(Rs), .clk(clock_1_out));  // open: en, clr
  Adder adder_1 (.a(Rs), .b(8'h1), .out(adder_1_out));  // open: cin, cout
  ROM #(.dataWidth(20)) rom_1 (.addr(Rs), .data({out_6[19:16], out_3, out_6[7:0]}));  // open: sel
  isShift isshift_1 (.in_1(out_6[19:16]), .out_2(isshift_1_out_2));
  assign bit_extender_1_out = {{4{1'b0}}, out_6[3:0]};  // Bit_Extender bit_extender_1
  Multiplexer #(.width(8), .enable("false")) multiplexer_1 (
    .in0(out_6[7:0]), .in1(bit_extender_1_out), .out(multiplexer_1_out), .sel(isshift_1_out_2));
  CU cu_1 (
    .OPcode(out_6[19:16]), .MemtoReg(cu_1_memtoreg), .RegDst(cu_1_regdst), .Jump(cu_1_jump),
    .MemWrite(cu_1_memwrite), .MemRead(cu_1_memread), .Branch(cu_1_branch), .ALUSrc(cu_1_alusrc),
    .RegWrite(cu_1_regwrite), .ALUop(cu_1_aluop), .BranchNEQ(cu_1_branchneq));
  Multiplexer #(.width(4), .enable("false")) multiplexer_2 (
    .in0(out_3[3:0]), .in1(out_6[7:4]), .out(multiplexer_2_out), .sel(cu_1_regdst));
  Register_File register_file_1 (
    .Rs(out_3[7:4]), .Rt(out_3[3:0]), .Rd(multiplexer_2_out), .WriteData(multiplexer_6_out),
    .RegWrite(cu_1_regwrite), .Read_Data_1(out_2), .Read_Data_2(out_5));
  Multiplexer #(.width(8), .enable("false")) multiplexer_3 (
    .in0(out_2), .in1(out_5), .out(multiplexer_3_out), .sel(isshift_1_out_2));
  ALU alu_1 (
    .Data1(multiplexer_3_out), .Data2(out_7), .ALUop(cu_1_aluop), .Zero(alu_1_zero),
    .ALU_result(alu_1_alu_result), .out_6(alu_1_out_6));
  Multiplexer #(.width(8), .enable("false")) multiplexer_4 (
    .in0(out_5), .in1(multiplexer_1_out), .out(out_7), .sel(cu_1_alusrc));
  and and_1 (and_1_out, cu_1_branch, alu_1_zero);
  Multiplexer #(.width(8), .enable("false")) multiplexer_5 (
    .in0(adder_1_out), .in1(multiplexer_1_out), .out(multiplexer_5_out), .sel(and_1_out));
  Data_Memory_Unit data_memory_unit_1 (
    .MemWrite(cu_1_memwrite), .Adress(alu_1_alu_result), .Write_Data(out_5), .MemRead(cu_1_memread),
    .Read_Data(data_memory_unit_1_read_data));
  Multiplexer #(.width(8), .enable("false")) multiplexer_6 (
    .in0(alu_1_alu_result), .in1(data_memory_unit_1_read_data), .out(multiplexer_6_out), .sel(cu_1_memtoreg));
  Multiplexer #(.width(8), .enable("false")) multiplexer_7 (
    .in0(multiplexer_5_out), .in1(out_3), .out(multiplexer_7_out), .sel(cu_1_jump));
  and and_2 (and_2_out, cu_1_branchneq, not_1_out);
  not not_1 (not_1_out, alu_1_zero);
  Multiplexer #(.width(8), .enable("false")) multiplexer_8 (
    .in0(multiplexer_7_out), .in1(multiplexer_1_out), .out(out_1), .sel(and_2_out));

  assign out_6[15:8] = out_3;

  // Notes on the sheet:
  //   contents of rom_1 (hex, n*v repeats v):
  //   406ff 40105 81205 d1240 e4106 21400 30152 5420 c2150 15420 a2200 72114 92103 b2203 60221 21300 962fc
  //   b61fc 21400 f1210
endmodule

module ALU (
  input  [7:0] Data1,
  input  [7:0] Data2,
  input  [2:0] ALUop,
  output Zero,
  output [7:0] ALU_result,
  output [2:0] out_6
);

  wire and_1_out, and_2_out, and_3_out, comparator_1_gt, not_1_out, not_2_out, or_1_out, or_2_out;
  wire [7:0] adder_1_out, and_4_out, multiplexer_2_out, nor_1_out, or_3_out, shifter_1_out, shifter_2_out,
       subtractor_1_out;
  wire [7:3] multiplexer_1_out;

  Comparator comparator_1 (.a(Data2), .b(8'h7), .gt(comparator_1_gt));  // open: eq, lt
  not not_1 (not_1_out, ALUop[1]);
  not not_2 (not_2_out, ALUop[0]);
  Multiplexer #(.width(8), .enable("false")) multiplexer_1 (
    .in0(Data2), .in1(8'h7), .out({multiplexer_1_out, out_6}), .sel(comparator_1_gt));
  and and_1 (and_1_out, ALUop[0], not_1_out, ALUop[2]);
  and and_2 (and_2_out, not_2_out, ALUop[1], ALUop[2]);
  or or_1 (or_1_out, Data2[3], Data2[4], Data2[5], Data2[6], Data2[7]);
  or or_2 (or_2_out, and_1_out, and_2_out);
  and and_3 (and_3_out, or_2_out, or_1_out);
  Adder adder_1 (.a(Data1), .b(Data2), .out(adder_1_out));  // open: cin, cout
  Subtractor subtractor_1 (.a(Data1), .b(Data2), .out(subtractor_1_out));  // open: bin, bout
  assign and_4_out = Data1 & Data2;  // AND_Gate and_4, 8 bits wide
  assign or_3_out = Data1 | Data2;  // OR_Gate or_3, 8 bits wide
  assign nor_1_out = ~(Data1 | Data2);  // NOR_Gate nor_1, 8 bits wide
  Shifter shifter_1 (.in(Data1), .\dist (out_6), .out(shifter_1_out));
  Shifter #(.shift("lr")) shifter_2 (.in(Data1), .\dist (out_6), .out(shifter_2_out));
  Multiplexer #(.select(3), .width(8), .enable("false")) multiplexer_2 (
    .in0(adder_1_out), .in1(subtractor_1_out), .in2(and_4_out), .in3(or_3_out), .in4(nor_1_out),
    .in5(shifter_1_out), .in6(shifter_2_out), .in7({8{1'b0}}), .out(multiplexer_2_out), .sel(ALUop));
  Multiplexer #(.width(8), .enable("false")) multiplexer_3 (
    .in0(multiplexer_2_out), .in1({8{1'b0}}), .out(ALU_result), .sel(and_3_out));
  nor nor_2 (Zero, ALU_result[0], ALU_result[1], ALU_result[2], ALU_result[3], ALU_result[4], ALU_result[5], ALU_result[6], ALU_result[7]);
endmodule

module Data_Memory_Unit (
  input  MemWrite,
  input  [7:0] Adress,
  input  [7:0] Write_Data,
  input  MemRead,
  output [7:0] Read_Data
);

  wire clock_1_out;

  Clock clock_1 (.out(clock_1_out));
  RAM #(.bus("separate")) ram_1 (
    .addr(Adress), .din(Write_Data), .data(Read_Data), .str(MemWrite), .clk(clock_1_out), .ld(MemRead));  // open: sel, clr
endmodule

module Control_Unit (
  input  [3:0] in_1,
  output RegWrite,
  output [2:0] ALUop
);

  wire and_1_out, and_2_out, and_3_out, and_4_out, and_5_out, and_6_out, and_7_out, and_8_out, and_9_out,
       and_10_out, and_11_out, not_1_out, not_2_out, not_3_out, not_4_out, not_5_out, not_6_out, not_7_out,
       not_8_out, not_9_out, not_10_out, xor_1_out;

  not not_1 (not_1_out, in_1[0]);
  not not_2 (not_2_out, in_1[1]);
  not not_3 (not_3_out, in_1[3]);
  and and_1 (and_1_out, not_1_out, not_2_out);
  xor xor_1 (xor_1_out, in_1[1], in_1[2]);
  not not_4 (not_4_out, in_1[0]);
  not not_5 (not_5_out, in_1[1]);
  not not_6 (not_6_out, in_1[2]);
  not not_7 (not_7_out, in_1[3]);
  not not_8 (not_8_out, in_1[2]);
  not not_9 (not_9_out, in_1[3]);
  not not_10 (not_10_out, in_1[0]);
  or or_1 (RegWrite, and_1_out, xor_1_out, not_3_out);
  and and_2 (and_2_out, not_4_out, not_5_out, not_6_out);
  and and_3 (and_3_out, in_1[0], in_1[1], not_7_out);
  and and_4 (and_4_out, not_4_out, in_1[2], in_1[3]);
  and and_5 (and_5_out, in_1[1], in_1[2], in_1[3]);
  and and_6 (and_6_out, in_1[1], in_1[2], not_7_out);
  and and_7 (and_7_out, in_1[0], in_1[2], not_7_out);
  and and_8 (and_8_out, in_1[1], not_4_out, not_6_out);
  and and_9 (and_9_out, not_4_out, not_5_out, in_1[2], in_1[3]);
  and and_10 (and_10_out, not_10_out, in_1[1], not_9_out);
  and and_11 (and_11_out, in_1[0], not_8_out, not_9_out);
  or or_2 (ALUop[2], and_10_out, and_11_out);
  or or_3 (ALUop[0], and_2_out, and_3_out, and_4_out, and_5_out);
  or or_4 (ALUop[1], and_6_out, and_7_out, and_8_out, and_9_out);
endmodule

module CU (
  input  [3:0] OPcode,
  output MemtoReg,
  output RegDst,
  output Jump,
  output MemWrite,
  output MemRead,
  output Branch,
  output ALUSrc,
  output RegWrite,
  output [2:0] ALUop,
  output BranchNEQ
);

  ROM #(.addrWidth(4), .dataWidth(12)) rom_1 (
    .addr(OPcode),
    .data({BranchNEQ, ALUop, RegWrite, ALUSrc, Branch, MemRead, MemWrite, Jump, RegDst, MemtoReg}));  // open: sel

  // Notes on the sheet:
  //   contents of rom_1 (hex, n*v repeats v):
  //   182 482 4 5c2 c0 282 6c2 3c2 1c0 48 2c0 d1 382 82 120 920
endmodule

module isShift (
  input  [3:0] in_1,
  output out_2
);

  wire and_1_out, and_2_out, not_1_out, not_2_out, not_3_out, not_4_out;

  not not_1 (not_1_out, in_1[3]);
  not not_2 (not_2_out, in_1[2]);
  not not_3 (not_3_out, in_1[1]);
  not not_4 (not_4_out, in_1[0]);
  and and_1 (and_1_out, not_1_out, not_2_out, in_1[1], in_1[0]);
  and and_2 (and_2_out, not_1_out, in_1[2], in_1[1], not_4_out);
  or or_1 (out_2, and_1_out, and_2_out);
endmodule
